# Fritzing sketch Thermometer Circuit Diagram (saved by Fritzing 0.9.3b)
circuit board: 11.5197cm x 8.75424cm
breadboards: 1

parts:
  Temperature_Sensor = TMP006 Thermopile Sensor
  Raspberry_Pi_3 = Raspberry Pi 3 [part_number=RPI-3-V1.2]

nets:
  VCC: Temperature_Sensor.VCC, Temperature_Sensor.ADDR1, Raspberry_Pi_3.3v3
  GND: Temperature_Sensor.GND, Raspberry_Pi_3.GND
  N1: Temperature_Sensor.SDA, Temperature_Sensor.ADDR0, Raspberry_Pi_3.GPIO2
  N2: Temperature_Sensor.SCL, Raspberry_Pi_3.GPIO3

custom parts:
  TMP006 Thermopile Sensor: Unlike all the other temperature sensors we have, this breakout has a really cool IR sensor from TI that can measure the temperature of an object without touching it! Simply point the sensor towards what you want to measure and it will detect the temperature by absorbing IR waves emitted. The embedded thermopile sensor generates a very very small voltage depending on how much IR there is, and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
